// Digital circuit TBOS Testing.dig as structural Verilog
module TBOS_Testing (
  input  clk
);

  wire button_1_out, button_2_out, button_3_out, telescope_computing_system_1_running;
  wire [15:0] Program_Files_d, Root_Drive_d, TBOS_2_3_d, telescope_computing_system_1_os_adr,
       telescope_computing_system_1_status_code;
  wire [16:0] keyboard_1_d;
  wire [18:0] telescope_computing_system_1_tk1_out;
  wire [19:0] telescope_computing_system_1_tnet_o_1, telescope_computing_system_1_tnet_o_2;
  wire [33:0] telescope_computing_system_1_d0_out, telescope_computing_system_1_d1_out;

  LED OS_Is_Running (.in(telescope_computing_system_1_running));
  // Probe Status on telescope_computing_system_1_status_code
  Button button_1 (.out(button_1_out));
  Telescope_Computing_System telescope_computing_system_1 (
    .Running(telescope_computing_system_1_running), .Status_Code(telescope_computing_system_1_status_code),
    .Power_On(button_1_out), .Clock_Input(clk), .Pause_CPU(button_2_out), .PAUS(1'b0), .STOP(button_3_out),
    .OS_Adr(telescope_computing_system_1_os_adr), .OS_In(TBOS_2_3_d), .D0_In(Root_Drive_d),
    .D0_Out(telescope_computing_system_1_d0_out), .D1_In(Program_Files_d),
    .D1_Out(telescope_computing_system_1_d1_out), .D2_In({16{1'b0}}), .D3_In({16{1'b0}}),
    .TNET_I_0({20{1'b0}}), .TNET_I_1(telescope_computing_system_1_tnet_o_1),
    .TNET_O_1(telescope_computing_system_1_tnet_o_1), .TNET_I_2(telescope_computing_system_1_tnet_o_2),
    .TNET_O_2(telescope_computing_system_1_tnet_o_2), .TNET_I_3({20{1'b0}}), .K0_In({17{1'b0}}),
    .TK1_Out(telescope_computing_system_1_tk1_out), .K1_In(keyboard_1_d), .K2_In({17{1'b0}}),
    .K3_In({17{1'b0}}), .GPI_0({18{1'b0}}), .GPI_1({18{1'b0}}), .GPI_2({18{1'b0}}), .GPI_3({18{1'b0}}));  // open: D2_Out, D3_Out, TNET_O_0, TNET_O_3, TK0_Out, TK2_Out, TK3_Out, GPO_0, GPO_1, GPO_2, GPO_3
  Button button_2 (.out(button_2_out));
  Button button_3 (.out(button_3_out));
  Keyboard keyboard_1 (
    .C(telescope_computing_system_1_tk1_out[18]), .en(telescope_computing_system_1_tk1_out[16]),
    .D(keyboard_1_d[15:0]), .av(keyboard_1_d[16]));
  // Probe OS Boot Address on telescope_computing_system_1_os_adr
  ROM #(.AddrBits(16), .Bits(16)) TBOS_2_3 (.A(telescope_computing_system_1_os_adr), .sel(1'b1), .D(TBOS_2_3_d));
  Terminal terminal_1 (
    .D(telescope_computing_system_1_tk1_out[15:0]), .C(telescope_computing_system_1_tk1_out[18]),
    .en(telescope_computing_system_1_tk1_out[17]));
  EEPROMDualPort #(.AddrBits(16), .Bits(16)) Root_Drive (
    .A(telescope_computing_system_1_d0_out[15:0]), .Din(telescope_computing_system_1_d0_out[31:16]),
    .str(telescope_computing_system_1_d0_out[32]), .C(telescope_computing_system_1_d0_out[33]), .ld(1'b1),
    .D(Root_Drive_d));
  EEPROMDualPort #(.AddrBits(16), .Bits(16)) Program_Files (
    .A(telescope_computing_system_1_d1_out[15:0]), .Din(telescope_computing_system_1_d1_out[31:16]),
    .str(telescope_computing_system_1_d1_out[32]), .C(telescope_computing_system_1_d1_out[33]), .ld(1'b1),
    .D(Program_Files_d));

  // Notes on the sheet:
  //   clk: Hz: 2048
  //   contents of TBOS_2_3 (hex, n*v repeats v):
  //   7c7,4600,252,520*0,32*1,38*0,a630,a730,50a0,f000,5090,1,50a0,e000
  //   ,3090,5010,7c7,5000,400,ae10,b912,5000,40,bb01,3078,b974,4600
  //   ,3a2,50a0,0,3078,b974,4600,5d7,d961,4a00,273,5000,ff00,4600,283
  //   ,3006,50a0,4,3078,b974,4600,3c6,50a0,f000,5090,2,b000,7000,64
  //   ,4600,28c,50a0,e800,3090,50a0,f000,3090,0,4600,289,b100,6000,62
  //   ,9200,4000,2fa,b100,6000,64,3060,b110,6011,63,b911,b150,af61,b901
  //   ,af01,cb06,4000,2ec,6020,66,d620,4a00,29c,d622,4a00,2c7,d624,4a00
  //   ,29c,6030,42,9931,4200,29c,b130,6033,65,60a3,8,d625,4200,2bd,4c00
  //   ,29c,4600,2bf,4d00,29c,3040,6000,2,3078,b974,4600,562,3004,7000
  //   ,64,bd0c,5010,86,a901,7000,65,60e0,a,50f0,2fe,50d0,200,60c0,b
  //   ,60a0,8,60b0,9,6070,7,6060,6,6050,5,6040,4,6030,3,6020,2,6010
  //   ,1,6000,0,1000,b951,db56,4800,2a1,b100,6000,24f,9200,4800,689
  //   ,5000,dead,4600,283,5000,600d,4600,283,7000,346,b100,6000,65,7010
  //   ,1,b110,6011,346,7010,0,7020,2,7030,3,7040,4,7050,5,7060,6,7070
  //   ,7,70b0,9,70e0,a,70a0,8,b1b0,5000,700,a10a,b508,db04,4000,28c
  //   ,db05,4000,69a,db06,4000,652,db07,4000,652,db01,4000,47f,db03
  //   ,4000,486,db00,4000,492,db02,4800,342,b100,6000,65,5010,ff03,7010
  //   ,6,4600,28c,5000,ff01,4600,283,0,b100,6000,64,6000,66,d602,4200
  //   ,28c,b100,6000,65,60b0,9,60a0,8,6070,7,6060,6,6050,5,6040,4,6030
  //   ,3,6020,2,6010,1,6000,0,1000,9210,4000,370,7090,0,b901,9b11,4800
  //   ,36a,3087,bbb1,704b,0,3040,5000,40,b110,b120,6032,206,cb10,4900
  //   ,39d,3061,b911,d514,4200,387,b921,b722,6032,206,c636,4200,37b
  //   ,3004,9b01,4000,39e,b911,d514,4200,396,b921,b722,6032,206,c631
  //   ,4a00,38b,5000,40,4600,37b,b060,604b,0,b9b1,3087,b120,6022,250
  //   ,4600,3ac,b120,6022,251,4600,3ac,7022,3b6,a910,3020,b524,6032
  //   ,206,cb01,4000,3c3,f000,b901,d504,4200,3b3,7032,206,b921,b722
  //   ,6032,206,4600,3b3,7032,206,3087,bbb1,704b,0,304a,b010,b911,6021
  //   ,2,d62f,4200,3cb,b130,b120,b62f,7021,2,7031,22,7031,42,6023,62
  //   ,b921,7022,62,6023,63,cb12,4100,3e6,7011,63,5020,1,7021,66,3021
  //   ,bd2c,5030,86,a923,b130,7032,0,7032,1,7032,2,7032,3,7032,4,7032
  //   ,5,7032,6,7032,7,7032,a,7032,9,3034,7032,8,7002,b,3001,3060,3047
  //   ,3078,b974,4600,415,3074,604b,0,b9b1,3087,9200,4000,445,6010,2
  //   ,5020,3e0,a022,a112,5020,7c00,a022,a112,b120,6022,64,3032,b43a
  //   ,a213,7010,2,6032,2,5010,1f,8113,4800,436,a230,7032,2,4600,445
  //   ,6021,2,5030,3e0,8132,4000,441,b535,3013,4600,436,b405,a220,7021
  //   ,2,3087,bbb1,704b,0,9200,4000,47b,6010,2,5020,7c00,a121,b52a,6032
  //   ,2,5040,1f,a143,cb40,4800,467,5040,1f,a044,a134,5040,3e0,a141
  //   ,b545,a234,7032,2,4600,47b,6024,2,5030,3e0,a132,b535,cb30,4000
  //   ,473,3043,4600,467,5030,3e0,a113,a033,a123,a221,7024,2,604b,0
  //   ,b9b1,3087,50a0,f000,5090,1111,0,4600,347,50a0,f000,5090,2222
  //   ,0,b100,3078,b974,4600,49d,4600,28c,5000,24e,3078,b974,4600,592
  //   ,50a0,f800,b190,4600,347,bbb1,707b,0,b110,3078,b974,4600,4b9,b100
  //   ,6000,63,9200,4000,4b3,6010,66,d610,4200,4b3,bb01,4600,4a8,7000
  //   ,63,607b,0,b9b1,3087,bbb2,704b,0,707b,1,3040,9210,4000,4ce,6020
  //   ,2,5000,3e0,8102,4000,4d2,b505,5070,4d2,4600,4b9,3078,b974,4600
  //   ,446,6014,66,d612,4a00,4ff,d613,4a00,4e0,b110,6011,24f,bb11,7011
  //   ,24f,6014,22,6021,0,b921,7021,0,b000,b120,6022,63,b921,b901,cb02
  //   ,4000,4ff,6030,22,cb31,4800,4ec,6030,42,cb31,4900,4ec,b931,7030
  //   ,42,4600,4ec,b110,7014,22,7014,42,6014,66,d611,4200,51b,3024,bd2c
  //   ,b92b,6022,86,3012,5030,400,ae13,5000,ff,a102,b408,ae03,3078,b974
  //   ,4600,3a7,6024,2,5030,1f,8123,4000,528,3002,b010,3078,b974,4600
  //   ,4b9,b100,7004,2,b100,6000,62,bb01,7000,62,b100,7004,66,604b,0
  //   ,607b,1,b9b2,3087,6020,0,bb21,7020,0,9220,4900,560,7001,22,7021
  //   ,42,6031,66,b632,5020,22a,cb02,4100,55a,5020,24f,cb02,4900,55a
  //   ,b120,6022,24f,b921,7022,24f,b633,7031,66,5060,1,4600,561,b160
  //   ,3087,6010,0,b911,7010,0,b010,b120,6022,63,b921,b911,cb12,4000
  //   ,591,6031,22,cb30,4800,56c,6031,42,b931,7031,42,9230,4800,56c
  //   ,7031,22,6031,66,b732,b734,d633,4a00,58d,b160,6066,24f,bb61,7066
  //   ,24f,b733,7031,66,4600,56c,3087,b010,b120,b911,5030,20,cb13,4000
  //   ,5b7,6031,22,cb30,4800,594,6061,66,b762,b764,d663,4a00,5ad,b130
  //   ,6033,24f,bb31,7033,24f,b763,7061,66,b130,7031,22,7031,42,b921
  //   ,4600,594,6010,0,a912,7010,0,3087,bbb3,707b,0,bd02,b110,b6ad,3091
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  //   Currently configured to run many tests.
  //   contents of Root_Drive (hex, n*v repeats v):
  //   16,4600,2,5000,0,50a0,800,b120,5010,1,2000,b911,2000,5000,3,50a0
  //   ,9000,2000,4d00,10,5000,2,2000
  //   contents of Program_Files (hex, n*v repeats v):
  //   8,4,1f,4,3f,4,51,0,16,4600,2,5000,0,50a0,800,b120,5010,1,2000
  //   ,b911,2000,5000,3,50a0,9000,2000,4d00,10,5000,2,2000,1f,4600,2
  //   ,5010,24,5000,3,50a0,4800,4500,d,2000,4d00,a,3029,cb21,4000,19
  //   ,50a0,8800,3092,2000,4c00,14,4600,6,50a0,9000,3092,2000,4600,1c
  //   ,11,4600,2,5000,3,50a0,8800,4500,b,2000,4d00,8,3019,50a0,4800
  //   ,3091,4600,4
endmodule
